# Fritzing sketch Geral (saved by Fritzing 0.9.5d)
breadboards: 1

parts:
  Componente1 = Arduino Uno (Rev3)
  Componente2 = Módulo Relé
  VALVE1 = Plastic Solenoid Valve
  Componente3 = Módulo Relé
  LED1 = LEDs [package=led10mm]
  Componente4 = Módulo Relé
  VALVE2 = Plastic Solenoid Valve
  ZS-042_RTC1 = ZS-042 RTC Module  # not connected

nets:
  5V: Componente1.5V, Componente2.5V, Componente3.5V, Componente4.5V
  GND: Componente1.GND, Componente2.GND, Componente3.GND, Componente4.GND
  N1: Componente2.NA, LED1.C
  N2: VALVE1.no_name_yet#1, Componente4.NF
  N3: Componente3.NA, VALVE2.no_name_yet#1

custom parts:
  Módulo Relé: Este modulo pode ser usado em diversos projetos afim de acionar cargas de até 250VAC @ 7A ou 125VAC @ 10A. Pode ser usado para controlar luzes, equipamentos ligados a rede elétrica, motores, etc. Você pode fazer uma ponte-H baseada em relés com alguns destes módulos.
  LEDs: LEDs Standard schematic elements and footprints for 5mm, 3mm, 1206, and 0603 sized LEDs. 5mm - Spark Fun Electronics SKU : COM-00529 (and others)
