# Fritzing sketch ModuloEnergia (saved by Fritzing 0.9.5d)
circuit board: 10.7836cm x 3.82684cm

parts:
  S1 = Screw terminal - 2 pins [package=THT]
  S2 = Screw terminal - 2 pins [package=THT]
  S3 = Screw terminal - 2 pins [package=THT]
  S4 = Screw terminal - 2 pins [package=THT]
  Entrada = Screw terminal - 2 pins [package=THT]
  S5 = screw terminal, 2 pins
  S6 = screw terminal, 2 pins
  S7 = screw terminal, 2 pins
  S8 = screw terminal, 2 pins
  E5 = screw terminal, 2 pins
  E6 = screw terminal, 2 pins
  E7 = screw terminal, 2 pins
  E8 = screw terminal, 2 pins
  E4 = Screw terminal - 2 pins [package=THT]
  E3 = Screw terminal - 2 pins [package=THT]
  E2 = Screw terminal - 2 pins [package=THT]
  E1 = Screw terminal - 2 pins [package=THT]

nets:
  N1: S1.pin1, S2.pin1, S3.pin1, S4.pin1, Entrada.pin1, S5.pin1, S6.pin1, S7.pin1, S8.pin1
  N2: S1.pin2, E1.pin2
  N3: S2.pin2, E2.pin2
  N4: S3.pin2, E3.pin2
  N5: S4.pin2, E4.pin2
  N6: Entrada.pin2, E5.pin1, E6.pin1, E7.pin1, E8.pin1, E4.pin1, E3.pin1, E2.pin1, E1.pin1
  N7: S5.pin2, E5.pin2
  N8: S6.pin2, E6.pin2
  N9: S7.pin2, E7.pin2
  N10: S8.pin2, E8.pin2
