# Fritzing sketch ModuloPrincipal (saved by Fritzing 0.9.5d)
circuit board: 11.3231cm x 10.252cm

parts:
  Nano = Arduino Nano (Rev3.0)
  Trêm = female pin header, 3 pins [form="♀ (female)"]
  Controlador_de_Relê = female pin header, 10 pins [form="♀ (female)"]
  Lampada = female pin header, 2 pins [form="♀ (female)"]
  Tela = female pin header, 4 pins [form="♀ (female)"]
  Relógio = female pin header, 4 pins [form="♀ (female)"]
  Reset = female pin header, 2 pins [form="♀ (female)"]
  Boia = Screw terminal - 2 pins [package=THT]
  Nível = screw terminal, 3 pins
  5V = Screw terminal - 2 pins [package=THT]

nets (from the pcb view):
  N1: Nano.RESET, Reset.pin2
  N2: Nano.GND, Controlador_de_Relê.pin10, Tela.pin1, Relógio.pin1, Reset.pin1, Nível.pin3, 5V.pin2
  N3: Nano.D2, Controlador_de_Relê.pin9
  N4: Nano.D3, Controlador_de_Relê.pin8
  N5: Nano.D4, Controlador_de_Relê.pin7
  N6: Nano.D5, Controlador_de_Relê.pin6
  N7: Nano.D6, Controlador_de_Relê.pin5
  N8: Nano.D7, Controlador_de_Relê.pin4
  N9: Nano.D8, Controlador_de_Relê.pin3
  N10: Nano.D9, Controlador_de_Relê.pin2
  N11: Nano.D10, Trêm.pin3
  N12: Nano.D11/MOSI, Trêm.pin2
  N13: Nano.D12/MISO, Trêm.pin1
  N14: Nano.5V, Controlador_de_Relê.pin1, Lampada.pin2, Tela.pin2, Relógio.pin2, Boia.pin1, Nível.pin1, 5V.pin1
  N15: Nano.A7, Nível.pin2
  N16: Nano.A6, Boia.pin2
  N17: Nano.A5, Tela.pin4, Relógio.pin4
  N18: Nano.A4, Tela.pin3, Relógio.pin3
  N19: Nano.D13/SCK, Lampada.pin1
